// Logisim project toysoc.circ as structural Verilog: 1 circuit, main circuit main
module main (
);

  wire and_1_out, and_2_out, and_3_out, and_4_out, and_5_out, and_6_out, and_7_out, and_8_out, and_9_out,
       and_10_out, and_11_out, and_12_out, and_13_out, button_1_out, clock_1_out, comparator_1_eq,
       comparator_2_eq, decoder_1_out0, decoder_1_out1, decoder_1_out2, decoder_1_out3, decoder_2_out0,
       decoder_2_out1, decoder_2_out2, decoder_2_out3, not_1_out, not_2_out, not_3_out, or_1_out, or_2_out,
       priority_encoder_1_out, priority_encoder_2_out, priority_encoder_3_out, priority_encoder_4_out;
  wire [2:0] demultiplexer_1_out0, demultiplexer_1_out1, demultiplexer_1_out2, demultiplexer_1_out3,
       multiplexer_2_out, multiplexer_3_out, multiplexer_4_out, multiplexer_5_out;
  wire [4:0] adder_1_out, cache_addr_q, multiplexer_1_out, PC_q;
  wire [7:0] cache_insn_q, multiplexer_6_out, multiplexer_7_out, multiplexer_8_out, rom_1_data, rom_2_data,
       rom_3_data, rom_4_data;

  Clock clock_1 (.out(clock_1_out));
  Button button_1 (.out(button_1_out));
  not not_1 (not_1_out, or_2_out);
  or or_1 (or_1_out, button_1_out, not_1_out);
  Register #(.width(5)) PC (.D(multiplexer_1_out), .en(or_1_out), .clk(clock_1_out), .Q(PC_q));  // open: clr
  Multiplexer #(.enable("false"), .width(5)) multiplexer_1 (
    .in0(adder_1_out), .in1(5'b01000), .out(multiplexer_1_out), .sel(button_1_out));
  Adder #(.width(5)) adder_1 (.a(5'b00001), .b(PC_q), .out(adder_1_out));  // open: cin, cout
  Decoder #(.enable("false"), .select(2)) decoder_1 (
    .out0(decoder_1_out0), .out1(decoder_1_out1), .out2(decoder_1_out2), .out3(decoder_1_out3),
    .sel(PC_q[4:3]));
  // Probe on PC_q[4:3]
  // Probe on PC_q[2:0]
  Demultiplexer #(.enable("false"), .select(2), .width(3)) demultiplexer_1 (
    .out0(demultiplexer_1_out0), .out1(demultiplexer_1_out1), .out2(demultiplexer_1_out2),
    .out3(demultiplexer_1_out3), .in(PC_q[2:0]), .sel(PC_q[4:3]));
  Decoder #(.enable("false"), .select(2)) decoder_2 (
    .out0(decoder_2_out0), .out1(decoder_2_out1), .out2(decoder_2_out2), .out3(decoder_2_out3),
    .sel(multiplexer_8_out[7:6]));
  // Probe on comparator_2_eq
  and and_1 (and_1_out, not_2_out, decoder_1_out0);
  and and_2 (and_2_out, not_2_out, decoder_1_out1);
  and and_3 (and_3_out, not_2_out, decoder_1_out2);
  and and_4 (and_4_out, not_2_out, decoder_1_out3);
  and and_5 (and_5_out, decoder_2_out0, comparator_2_eq);
  and and_6 (and_6_out, decoder_2_out1, comparator_2_eq);
  and and_7 (and_7_out, decoder_2_out2, comparator_2_eq);
  and and_8 (and_8_out, decoder_2_out3, comparator_2_eq);
  // Probe on or_2_out
  or or_2 (or_2_out, and_9_out, and_10_out, and_11_out, and_12_out);
  Priority_Encoder #(.select(1)) priority_encoder_1 (
    .in0(and_5_out), .in1(and_1_out), .out(priority_encoder_1_out));  // open: gs, en_out, en_in
  and and_9 (and_9_out, and_1_out, and_5_out);
  Priority_Encoder #(.select(1)) priority_encoder_2 (
    .in0(and_6_out), .in1(and_2_out), .out(priority_encoder_2_out));  // open: gs, en_out, en_in
  and and_10 (and_10_out, and_2_out, and_6_out);
  Priority_Encoder #(.select(1)) priority_encoder_3 (
    .in0(and_7_out), .in1(and_3_out), .out(priority_encoder_3_out));  // open: gs, en_out, en_in
  and and_11 (and_11_out, and_3_out, and_7_out);
  Priority_Encoder #(.select(1)) priority_encoder_4 (
    .in0(and_8_out), .in1(and_4_out), .out(priority_encoder_4_out));  // open: gs, en_out, en_in
  and and_12 (and_12_out, and_4_out, and_8_out);
  ROM #(.addrWidth(3)) rom_1 (.addr(multiplexer_2_out), .data(rom_1_data));
  Multiplexer #(.enable("false"), .width(3)) multiplexer_2 (
    .in0(multiplexer_8_out[5:3]), .in1(demultiplexer_1_out0), .out(multiplexer_2_out),
    .sel(priority_encoder_1_out));
  ROM #(.addrWidth(3)) rom_2 (.addr(multiplexer_3_out), .data(rom_2_data));
  Multiplexer #(.enable("false"), .width(3)) multiplexer_3 (
    .in0(multiplexer_8_out[5:3]), .in1(demultiplexer_1_out1), .out(multiplexer_3_out),
    .sel(priority_encoder_2_out));
  ROM #(.addrWidth(3)) rom_3 (.addr(multiplexer_4_out), .data(rom_3_data));
  Multiplexer #(.enable("false"), .width(3)) multiplexer_4 (
    .in0(multiplexer_8_out[5:3]), .in1(demultiplexer_1_out2), .out(multiplexer_4_out),
    .sel(priority_encoder_3_out));
  ROM #(.addrWidth(3)) rom_4 (.addr(multiplexer_5_out), .data(rom_4_data));
  Multiplexer #(.enable("false"), .width(3)) multiplexer_5 (
    .in0(multiplexer_8_out[5:3]), .in1(demultiplexer_1_out3), .out(multiplexer_5_out),
    .sel(priority_encoder_4_out));
  Register #(.width(5)) cache_addr (.D(PC_q), .en(1'b1), .clk(clock_1_out), .Q(cache_addr_q), .clr(button_1_out));
  Comparator #(.width(5)) comparator_1 (.a(PC_q), .b(cache_addr_q), .eq(comparator_1_eq));  // open: gt, lt
  Register cache_insn (.D(multiplexer_7_out), .en(1'b1), .clk(clock_1_out), .Q(cache_insn_q), .clr(button_1_out));
  Multiplexer #(.enable("false"), .select(2), .width(8)) multiplexer_6 (
    .in0(rom_1_data), .in1(rom_2_data), .in2(rom_3_data), .in3(rom_4_data), .out(multiplexer_6_out),
    .sel(multiplexer_8_out[7:6]));
  Multiplexer #(.enable("false"), .select(2), .width(8)) multiplexer_7 (
    .in0(rom_1_data), .in1(rom_2_data), .in2(rom_3_data), .in3(rom_4_data), .out(multiplexer_7_out),
    .sel(PC_q[4:3]));
  not not_2 (not_2_out, comparator_1_eq);
  Multiplexer #(.enable("false"), .width(8)) multiplexer_8 (
    .in0(cache_insn_q), .in1(multiplexer_7_out), .out(multiplexer_8_out), .sel(not_2_out));
  // Probe on multiplexer_8_out
  Comparator #(.width(3)) comparator_2 (.a(3'b100), .b(multiplexer_8_out[2:0]), .eq(comparator_2_eq));  // open: gt, lt
  // Probe on multiplexer_8_out[7:6]
  // Probe on multiplexer_8_out[5:3]
  // Probe on multiplexer_6_out
  // Probe on and_13_out
  not not_3 (not_3_out, or_2_out);
  and and_13 (and_13_out, not_3_out, comparator_2_eq);

  // Notes on the sheet:
  //   contents of rom_1 (hex, n*v repeats v):
  //   0 1 2 3 4 5 6 7
  //   contents of rom_2 (hex, n*v repeats v):
  //   0 1c 7c 4*0 ff
endmodule
